# Fritzing sketch 7SegI2C (saved by Fritzing 0.9.3b)
circuit board: 6cm x 5cm

parts:
  7_Segment1 = 7 Segment Display
  7_Segment2 = 7 Segment Display
  J1 = female pin header, 4 pins [form="♀ (female)"]
  R3 = Resistor [tolerance=±5% resistance=220 package=THT]
  R4 = Resistor [tolerance=±5% resistance=220 package=THT]
  R5 = Resistor [tolerance=±5% resistance=220 package=THT]
  R6 = Resistor [tolerance=±5% resistance=220 package=THT]
  R7 = Resistor [tolerance=±5% resistance=220 package=THT]
  R8 = Resistor [tolerance=±5% resistance=220 package=THT]
  R9 = Resistor [tolerance=±5% resistance=220 package=THT]
  R10 = Resistor [tolerance=±5% resistance=220 package=THT]
  R11 = Resistor [tolerance=±5% resistance=220 package=THT]
  R12 = Resistor [tolerance=±5% resistance=220 package=THT]
  R13 = Resistor [tolerance=±5% resistance=220 package=THT]
  R14 = Resistor [tolerance=±5% resistance=220 package=THT]
  R15 = Resistor [tolerance=±5% resistance=220 package=THT]
  R16 = Resistor [tolerance=±5% resistance=220 package=THT]
  R17 = Resistor [tolerance=±5% resistance=220 package=THT]
  R18 = Resistor [tolerance=±5% resistance=220 package=THT]
  R19 = Resistor [tolerance=±5% resistance=220 package=THT]
  MCP23017 = MCP23017 I2C I/O Expander

nets:
  N1: 7_Segment1.Segment_A#1, R9.Pin_1
  N2: 7_Segment1.Segment_F, R8.Pin_1
  N3: 7_Segment1.Segment_E, R7.Pin_1
  N4: 7_Segment1.Segment_D, R6.Pin_1
  N5: 7_Segment1.Segment_DP, R10.Pin_1
  N6: 7_Segment1.Segment_C, R5.Pin_1
  GND: 7_Segment1.common_cathode, 7_Segment2.common_cathode, J1.pin2, MCP23017.VSS, MCP23017.A0, MCP23017.A1, MCP23017.A2
  N7: 7_Segment1.Segment_B, R4.Pin_1
  N8: 7_Segment1.Segment_A#10, R3.Pin_1
  N9: 7_Segment2.Segment_A#1, R17.Pin_1
  N10: 7_Segment2.Segment_F, R16.Pin_1
  N11: 7_Segment2.Segment_E, R15.Pin_1
  N12: 7_Segment2.Segment_D, R14.Pin_1
  N13: 7_Segment2.Segment_DP, R18.Pin_1
  N14: 7_Segment2.Segment_C, R13.Pin_1
  N15: 7_Segment2.Segment_B, R12.Pin_1
  N16: 7_Segment2.Segment_A#10, R11.Pin_1
  5V: J1.pin1, R19.Pin_1, MCP23017.VDD
  N17: J1.pin3, MCP23017.SCL
  N18: J1.pin4, MCP23017.SDA
  N19: R3.Pin_0, MCP23017.GPB0
  N20: R4.Pin_0, MCP23017.GPB1
  N21: R5.Pin_0, MCP23017.GPB2
  N22: R6.Pin_0, MCP23017.GPB3
  N23: R7.Pin_0, MCP23017.GPB4
  N24: R8.Pin_0, MCP23017.GPB5
  N25: R9.Pin_0, MCP23017.GPB6
  N26: R10.Pin_0, MCP23017.GPB7
  N27: R11.Pin_0, MCP23017.GPA0
  N28: R12.Pin_0, MCP23017.GPA1
  N29: R13.Pin_0, MCP23017.GPA2
  N30: R14.Pin_0, MCP23017.GPA3
  N31: R15.Pin_0, MCP23017.GPA4
  N32: R16.Pin_0, MCP23017.GPA5
  N33: R17.Pin_0, MCP23017.GPA6
  N34: R18.Pin_0, MCP23017.GPA7
  N35: R19.Pin_0, MCP23017.RESET

custom parts:
  MCP23017 I2C I/O Expander: The MCP23017 uses two i2c pins (these can be shared with other i2c devices), and in exchange gives you 16 general purpose pins. You can set each of 16 pins to be input, output, input with a pullup or open drain. There's even the ability to get an interrupt via an external pin when any of the inputs change so you don't have to keep polling the chip.
