# Fritzing sketch AtTinyI2C (saved by Fritzing 0.9.3b)
circuit board: 2.6cm x 2.5cm

parts:
  U1 = attiny85 [package=dip]
  R2 = Resistor [tolerance=±5% resistance=4.7k package=THT]
  J2 = female pin header, 4 pins [form="♀ (female)"]
  J1 = male pin header, 6 pins [form="♂ (male)"]
  R1 = Resistor [tolerance=±5% resistance=4.7k package=THT]

nets:
  N1: U1.Pin_2, J1.pin5
  N2: U1.Pin_3, J1.pin4
  N3: U1.Pin_4, J2.pin3, J1.pin2
  N4: U1.Pin_5, R2.Pin_0, J2.pin1
  N5: U1.Pin_6, J1.pin1
  N6: U1.Pin_7, J2.pin2, R1.Pin_0
  N7: U1.Pin_8, R2.Pin_1, J2.pin4, J1.pin6, R1.Pin_1

notes:
  SCL
  SDA
