# Fritzing sketch Board (saved by Fritzing 0.9.3b)

parts:
  MKR1000 = Arduino MKR1000
  J4 = female pin header, 7 pins [form="♀ (female)"]
  J3 = female pin header, 7 pins [form="♀ (female)"]
  J2 = female pin header, 7 pins [form="♀ (female)"]
  J1 = female pin header, 7 pins [form="♀ (female)"]
  U1 = Voltage Regulator - 5V [package="TO220 [THT]"]
  Levelshifter = I2C level shifter bidirectional
  Power_plug1 = Power plug
  D1 = Diode [package=diode-1n4148]
  D2 = Diode [package=diode-1n4148]
  D3 = Diode [package=diode-1n4148]
  D4 = Diode [package=diode-1n4148]

nets:
  N1: MKR1000.D0, Levelshifter.LV3
  N2: MKR1000.D1, Levelshifter.LV4
  Zeile 1: MKR1000.D2_PWM, J2.pin5, J1.pin5
  Zeile 2: MKR1000.D3_PWM, J4.pin5, J3.pin5
  Spalte 1: MKR1000.D4_PWM, J3.pin6, J1.pin6
  Spalte 2: MKR1000.D5_PWM, J4.pin6, J2.pin6
  GND: MKR1000.GND, J4.pin7, J3.pin7, J2.pin7, J1.pin7, U1.GND, Levelshifter.GND, Power_plug1.GND
  3.3V: MKR1000.VCC, Levelshifter.LV
  5V: MKR1000.VIN, J4.pin4, J3.pin4, J2.pin4, J1.pin4, U1.output_voltage, Levelshifter.HV
  Rx Chip: J4.pin1, J3.pin1, J2.pin1, J1.pin1, Levelshifter.HV3
  N3: J4.pin2, D2.C
  N4: J3.pin2, D1.C
  N5: J2.pin2, D3.C
  N6: J1.pin2, D4.C
  N7: U1.input_voltage, Power_plug1.VCC
  N8: Levelshifter.HV4, D1.A, D2.A, D3.A, D4.A

notes:
  cyan /blau = Kommunikations leitung
  gelb = Spalten Lokalisieren
  grau = Zeilen Lokalisieren

custom parts:
  Arduino MKR1000: MKR1000 is a powerful board that combines the functionality of the Zero and the Wi-Fi Shield. It is the ideal solution for makers wanting to design IoT projects with minimal previous experience in networking
