# Fritzing sketch Boardv2 (saved by Fritzing 0.9.3b)
circuit board: 9.5cm x 6.5cm

parts:
  MKR1000 = Arduino MKR1000
  Levelshifter = I2C level shifter bidirectional
  D1 = Diode [package=diode-1n4148]
  D2 = Diode [package=diode-1n4148]
  D3 = Diode [package=diode-1n4148]
  D4 = Diode [package=diode-1n4148]
  IC1 = 4011 4 x 2 Input NAND Gate, single part [part_number=4011 package="DIP (Dual Inline) [THT]"]
  J2 = female pin header, 6 pins [form="♀ (female)"]
  J3 = female pin header, 6 pins [form="♀ (female)"]
  J5 = male pin header, 2 pins [form="♂ (male)"]
  J4 = female pin header, 6 pins [form="♀ (female)"]
  S1 = Pushbutton [package="[THT]"]
  J6 = female pin header, 6 pins [form="♀ (female)"]
  J1 = female pin header, 6 pins [form="♀ (female)"]

nets:
  N1: MKR1000.A1, S1.Pin_3, S1.Pin_4
  N2: MKR1000.D0, Levelshifter.LV2
  N3: MKR1000.D1, Levelshifter.LV1
  Zeile 1: MKR1000.D2_PWM, IC1.B3, IC1.B4
  Zeile 2: MKR1000.D3_PWM, IC1.A1, IC1.A2
  Spalte 1: MKR1000.D4_PWM, IC1.B1, IC1.A4
  Spalte 2: MKR1000.D5_PWM, IC1.B2, IC1.A3
  GND: MKR1000.GND, Levelshifter.GND, IC1.GND, J2.pin5, J3.pin5, J5.pin2, J4.pin5, S1.Pin_1, S1.Pin_2, J6.pin5, J1.pin5
  3.3V: MKR1000.VCC, Levelshifter.LV
  5V: MKR1000.VIN, Levelshifter.HV, IC1.VDD, J2.pin1, J3.pin1, J5.pin1, J4.pin1, J6.pin1, J6.pin6, J1.pin1
  N4: Levelshifter.HV1, D1.A, D2.A, D3.A, D4.A
  Rx Chip: Levelshifter.HV2, J2.pin2, J3.pin2, J4.pin2, J6.pin2, J1.pin2
  N5: D1.C, J3.pin3
  N6: D2.C, J4.pin3
  N7: D3.C, J2.pin3
  N8: D4.C, J1.pin3
  Chip 1: IC1.Q1, J1.pin6
  Chip 3: IC1.Q2, J3.pin6
  Chip 4: IC1.Q3, J4.pin6
  Chip 2: IC1.Q4, J2.pin6

notes:
  cyan /blau = Kommunikations leitung
  gelb = Spalten Lokalisieren
  grau = Zeilen Lokalisieren

custom parts:
  Arduino MKR1000: MKR1000 is a powerful board that combines the functionality of the Zero and the Wi-Fi Shield. It is the ideal solution for makers wanting to design IoT projects with minimal previous experience in networking
