# Fritzing sketch ChipButton (saved by Fritzing 0.9.3b)
circuit board: 2.5cm x 2.5cm

parts:
  AtTiny = attiny85 [package=dip]
  S1 = Pushbutton [package="[THT]"]
  R1 = Resistor [tolerance=±5% resistance=220 package=THT]
  J1 = male pin header, 6 pins [form="♂ (male)"]

nets:
  N1: AtTiny.Pin_2, J1.pin5
  N2: AtTiny.Pin_3, J1.pin4
  N3: AtTiny.Pin_4, S1.Pin_1, S1.Pin_2, J1.pin2
  N4: AtTiny.Pin_6, J1.pin1
  N5: AtTiny.Pin_7, R1.Pin_0
  N6: AtTiny.Pin_8, J1.pin6
  N7: S1.Pin_3, S1.Pin_4, R1.Pin_1

notes:
  Chip mit Button,
  mit akuteller Localisations Schaltung
