# Fritzing sketch ChipButtonAktuell (saved by Fritzing 0.9.3b)
circuit board: 2.71221cm x 2.20642cm

parts:
  U1 = attiny85 [package=dip]
  S1 = Pushbutton [package="[THT]"]
  R1 = Resistor [tolerance=±5% resistance=220 package=THT]
  J1 = male pin header, 7 pins [form="♂ (male)"]

nets:
  N1: U1.Pin_2, J1.pin3
  N2: U1.Pin_3, J1.pin2
  N3: U1.Pin_4, R1.Pin_0, J1.pin1
  N4: U1.Pin_5, S1.Pin_1
  N5: U1.Pin_6, J1.pin7
  N6: U1.Pin_7, J1.pin6
  N7: U1.Pin_8, J1.pin4
  N8: S1.Pin_3, S1.Pin_4, R1.Pin_1

notes:
  Chip mit Button,
  mit akuteller Localisations Schaltung
