# Fritzing sketch ChipLED (saved by Fritzing 0.9.3b)
circuit board: 2.5cm x 2.5cm

parts:
  AtTiny = attiny85 [package=dip]
  R1 = Resistor [tolerance=±5% resistance=150 package=THT]
  J1 = male pin header, 6 pins [form="♂ (male)"]
  LED1 = LED - 5mm [color="Red (633nm)" package="5 mm [THT]"]

nets:
  N1: AtTiny.Pin_2, J1.pin5
  N2: AtTiny.Pin_3, J1.pin4
  N3: AtTiny.Pin_4, J1.pin2, LED1.anode
  N4: AtTiny.Pin_5, R1.Pin_0
  N5: AtTiny.Pin_6, J1.pin1
  N6: AtTiny.Pin_8, J1.pin6
  N7: R1.Pin_1, LED1.cathode

notes:
  Chip mit LED,
  mit akuteller Localisations Schaltung
  Rx
  Tx
