# Fritzing sketch ChipLEDAktuell (saved by Fritzing 0.9.3b)
circuit board: 2.42642cm x 2.11299cm

parts:
  U1 = attiny85 [package=dip]
  R1 = Resistor [tolerance=±5% resistance=150 package=THT]
  LED1 = LED - 5mm [color="Red (633nm)" package="5 mm [THT]"]
  J1 = male pin header, 7 pins [form="♂ (male)"]

nets:
  N1: U1.Pin_2, J1.pin3
  N2: U1.Pin_3, J1.pin2
  N3: U1.Pin_4, R1.Pin_0, J1.pin1
  N4: U1.Pin_5, LED1.cathode
  N5: U1.Pin_6, J1.pin7
  N6: U1.Pin_7, J1.pin6
  N7: U1.Pin_8, J1.pin4
  N8: R1.Pin_1, LED1.anode

notes:
  Chip mit LED,
  mit alter Localisations Schaltung
