# Fritzing sketch LocationTest (saved by Fritzing 0.9.3b)

parts:
  Bauteil1 = Arduino Nano (Rev3.0)
  Bauteil2 = Arduino Nano (Rev3.0)
  Bauteil3 = Arduino Nano (Rev3.0)
  U1 = attiny85 [package=dip]
  U2 = attiny85 [package=dip]
  U3 = attiny85 [package=dip]
  Q1 = Basic FET N-Channel [package="TO220 [THT]"]

nets:
  N1: Bauteil1.D8, U1.Pin_2
  N2: Bauteil1.D9, U1.Pin_3
  N3: Bauteil1.A5, U1.Pin_8
  N4: Bauteil1.A4, U1.Pin_4
  N5: Bauteil2.D8, U2.Pin_2
  N6: Bauteil2.D9, U2.Pin_3
  N7: Bauteil2.GND, U2.Pin_4
  N8: Bauteil2.5V, Q1.gate
  N9: Bauteil2.A5, Q1.drain
  N10: Bauteil3.D8, U3.Pin_2
  N11: Bauteil3.D9, U3.Pin_3
  N12: Bauteil3.GND, U3.Pin_4
  N13: Bauteil3.5V, U3.Pin_8
  N14: Bauteil3.A5, U3.Pin_7
  N15: Bauteil3.A4, U3.Pin_5
  N16: U2.Pin_8, Q1.source
