# Fritzing sketch NanoI2C (saved by Fritzing 0.9.3b)
circuit board: 3.5cm x 4.5cm

parts:
  Bauteil1 = Arduino Nano (Rev3.0)
  J2 = female pin header, 4 pins [form="♀ (female)"]
  J1 = male pin header, 6 pins [form="♂ (male)"]

nets:
  N1: Bauteil1.GND, J2.pin2, J1.pin5
  N2: Bauteil1.D5, J1.pin6
  N3: Bauteil1.D8, J1.pin3
  N4: Bauteil1.D9, J1.pin2
  N5: Bauteil1.VIN, J2.pin1, J1.pin1
  N6: Bauteil1.A5, J2.pin3
  N7: Bauteil1.A4, J2.pin4
