# Fritzing sketch TestDisplay (saved by Fritzing 0.9.3b)

parts:
  Bauteil1 = Arduino MKR1000
  Bauteil2 = I2C level shifter bidirectional
  U1 = attiny85 [package=dip]
  Bauteil3 = Arduino Nano (Rev3.0)
  D1 = Diode [package=diode-1n4001]
  D2 = Diode [package=diode-1n4001]

nets:
  N1: Bauteil1.D0, Bauteil2.LV2
  N2: Bauteil1.D1, Bauteil2.LV1
  GND: Bauteil1.GND, Bauteil2.GND, U1.Pin_4, Bauteil3.GND
  N3: Bauteil1.VCC, Bauteil2.LV
  5V: Bauteil1.5V, Bauteil2.HV, U1.Pin_8, Bauteil3.VIN
  N4: Bauteil2.HV1, D1.A, D2.A
  N5: Bauteil2.HV2, U1.Pin_2, Bauteil3.D11/MOSI
  N6: U1.Pin_3, D1.C
  N7: Bauteil3.D10, D2.C

custom parts:
  Arduino MKR1000: MKR1000 is a powerful board that combines the functionality of the Zero and the Wi-Fi Shield. It is the ideal solution for makers wanting to design IoT projects with minimal previous experience in networking
