# Fritzing sketch UmsteckerOLED (saved by Fritzing 0.9.3b)
circuit board: 1cm x 2cm

parts:
  J2 = female pin header, 4 pins [form="♀ (female)"]
  J1 = female pin header, 4 pins [form="♀ (female)"]

nets:
  N1: J2.pin1, J1.pin4
  N2: J2.pin2, J1.pin3
  N3: J2.pin3, J1.pin2
  N4: J2.pin4, J1.pin1
