# Fritzing sketch WS2812bShield (saved by Fritzing 0.9.3b)
circuit board: 4.5cm x 4cm

parts:
  J1 = male pin header, 3 pins [form="♂ (male)"]
  C1 = Electrolytic Capacitor [capacitance=10µF package="100 mil [THT, electrolytic]"]
  C2 = Electrolytic Capacitor [capacitance=1µF package="100 mil [THT, electrolytic]"]
  R1 = Resistor [tolerance=±5% resistance=220 package=THT]
  J2 = male pin header, 4 pins [form="♂ (male)"]

nets:
  N1: J1.pin1, C1.+, C2.+, J2.pin4
  N2: J1.pin2, R1.Pin_0
  N3: J1.pin3, C1.-, C2.-, J2.pin3
  N4: R1.Pin_1, J2.pin2
